// Logisim project Aula01_Somador.circ as structural Verilog: 2 circuits, main circuit MeioSomador
module MeioSomador (
  input  A,
  input  B,
  output Soma,
  output Cout
);

  xor xor_1 (Soma, A, B);
  and and_1 (Cout, A, B);
endmodule

module SomadorCompleto (
  input  in_1,
  input  in_2,
  input  in_3,
  output out_4,
  output out_5
);

  wire meiosomador_1_cout, meiosomador_1_soma, meiosomador_2_cout;

  MeioSomador meiosomador_1 (.Cout(meiosomador_1_cout), .B(in_2), .A(in_1), .Soma(meiosomador_1_soma));
  MeioSomador meiosomador_2 (.Cout(meiosomador_2_cout), .B(in_3), .A(meiosomador_1_soma), .Soma(out_4));
  or or_1 (out_5, meiosomador_2_cout, meiosomador_1_cout);
endmodule
