// Logisim project Aula01_Subtrator.circ as structural Verilog: 2 circuits, main circuit MeioSubtrator
module MeioSubtrator (
  input  A,
  input  B,
  output S,
  output Bout
);

  wire not_1_out;

  not not_1 (not_1_out, A);
  xor xor_1 (S, A, B);
  and and_1 (Bout, B, not_1_out);
endmodule

module SubtratorCompleto (
  input  in_1,
  input  in_2,
  input  in_3,
  output out_4,
  output out_5
);

  wire meiosubtrator_1_bout, meiosubtrator_1_s, meiosubtrator_2_bout;

  MeioSubtrator meiosubtrator_1 (.Bout(meiosubtrator_1_bout), .S(meiosubtrator_1_s), .A(in_1), .B(in_2));
  MeioSubtrator meiosubtrator_2 (.Bout(meiosubtrator_2_bout), .S(out_4), .A(meiosubtrator_1_s), .B(in_3));
  or or_1 (out_5, meiosubtrator_2_bout, meiosubtrator_1_bout);
endmodule
