// Logisim project Relatorio1.circ as structural Verilog: 1 circuit, main circuit main
module main (
  input  [1:0] in_1,
  input  in_2,
  input  [2:0] in_3,
  input  in_4,
  output [1:0] out_5,
  output [1:0] out_6
);

  wire [1:0] demultiplexer_1_out0, demultiplexer_1_out1, meiosomador_1_soma, meiosubtrator_1_s,
       somadorcompleto_1_out_4, subtratorcompleto_1_out_4;
  wire [2:0] demultiplexer_2_out0, demultiplexer_2_out1;

  Demultiplexer #(.width(2), .enable("false")) demultiplexer_1 (
    .out0(demultiplexer_1_out0), .out1(demultiplexer_1_out1), .in(in_1), .sel(in_2));
  Demultiplexer #(.width(3), .enable("false")) demultiplexer_2 (
    .out0(demultiplexer_2_out0), .out1(demultiplexer_2_out1), .in(in_3), .sel(in_4));
  MeioSomador meiosomador_1 (
    .Cout(meiosomador_1_soma[1]), .B(demultiplexer_1_out0[1]), .A(demultiplexer_1_out0[0]),
    .Soma(meiosomador_1_soma[0]));
  MeioSubtrator meiosubtrator_1 (
    .Bout(meiosubtrator_1_s[1]), .S(meiosubtrator_1_s[0]), .A(demultiplexer_1_out1[0]),
    .B(demultiplexer_1_out1[1]));
  SomadorCompleto somadorcompleto_1 (
    .out_4(somadorcompleto_1_out_4[0]), .in_2(demultiplexer_2_out0[1]), .in_1(demultiplexer_2_out0[0]),
    .in_3(demultiplexer_2_out0[2]), .out_5(somadorcompleto_1_out_4[1]));
  SubtratorCompleto subtratorcompleto_1 (
    .out_5(subtratorcompleto_1_out_4[1]), .out_4(subtratorcompleto_1_out_4[0]),
    .in_3(demultiplexer_2_out1[2]), .in_2(demultiplexer_2_out1[1]), .in_1(demultiplexer_2_out1[0]));
  Multiplexer #(.width(2), .enable("false")) multiplexer_1 (
    .in0(meiosomador_1_soma), .in1(meiosubtrator_1_s), .out(out_5), .sel(in_2));
  Multiplexer #(.width(2), .enable("false")) multiplexer_2 (
    .in0(somadorcompleto_1_out_4), .in1(subtratorcompleto_1_out_4), .out(out_6), .sel(in_4));
endmodule
